# Fritzing sketch Cellucon.Arduino.mini (saved by Fritzing 0.9.3b)

parts:
  Arduino_Pro_Mini = Arduino Pro Mini v13
  RC-Rudder = Basic Servo
  J2 = Dagu DGServo 9g header (male) [package=THT]
  J1 = Dagu DGServo 9g header (male) [package=THT]
  S2 = Dagu DGServo 9g header connector (female) [package=THT]
  S1 = Dagu DGServo 9g header connector (female) [package=THT]
  RN42 = Bluetooth Module Breakout - Roving Networks (RN-41)
  C1 = Electrolytic Capacitor [capacitance=47µF voltage=10V package="100 mil [THT, electrolytic]"]
  C2 = Ceramic Capacitor [capacitance=100nF voltage=50V package="100 mil [THT, multilayer]"]
  R7 = Resistor [tolerance=±5% resistance=10k package=THT]
  LP2950L-3_3V = Voltage Regulator [package=to-92]
  U2 = LIPO-1000mAh [package=lipo-1000]
  Motor_Power_(ESC) = ESC MLF1218
  M1 = DC Motor

nets:
  N1: Arduino_Pro_Mini.D0/TX, R7.Pin_1
  N2: Arduino_Pro_Mini.D1/RX, RN42.UARTTX
  VCC: Arduino_Pro_Mini.VCC, J2.Vcc, J1.Vcc, C2.0, LP2950L-3_3V.IN
  N3: Arduino_Pro_Mini.D10_PWM/SS, J1.pulse
  N4: Arduino_Pro_Mini.D9_PWM, J2.pulse
  GND: Arduino_Pro_Mini.GND, J2.gnd, J1.gnd, RN42.GND, C1.-, C2.1, LP2950L-3_3V.GND
  GND_2: RC-Rudder.gnd, S2.gnd
  VCC_2: RC-Rudder.vcc, S2.Vcc
  N5: RC-Rudder.pulse, S2.pulse
  GND_3: S1.gnd, U2.-, Motor_Power_(ESC).GND, Motor_Power_(ESC).GND*, M1.pin_2
  N6: S1.Vcc, Motor_Power_(ESC).+5
  N7: S1.pulse, Motor_Power_(ESC).PPM
  N8: RN42.VCC, C1.+, LP2950L-3_3V.OUT
  N9: RN42.UARTRX, R7.Pin_0
  N10: U2.+, Motor_Power_(ESC).V+
  N11: Motor_Power_(ESC).U, M1.pin_1

notes:
  CelluCon-Mini
  2017.11.02

custom parts:
  Voltage Regulator: Voltage Regulator Standard 7805 5V regulator. IGO (Input Ground Output). Spark Fun Electronics SKU : COM-00107
  ESC MLF1218: ESC (Electronic Speed Control) for Cheerson CX-20 quadcopter

// code stored in the sketch: Untitled.ino




// ????????????????


/*

  http://tetsuakibaba.jp/index.php?page=workshop/ServoBasis/main

  ?????????????????

  r: ????????

  800-2200: 0??90???



  a: attach(9)

  d: detach()



  http://marupeke296.com/EL_Ard_No9_ServoMotor.html

  http://www.vstone.co.jp/vs_wiki/main/wiki.cgi?page=Arduino%A4%C7%BB%CF%A4%E1%A4%EB%A5%ED%A5%DC%A5%C3%A5%C8%C0%A9%B8%E6

  http://wacho.main.jp/Elec/Servo_Driver/Servo_Driver.html

  http://detail.chiebukuro.yahoo.co.jp/qa/question_detail/q14109772659

  http://otonaradicon.com/arrc/



  ????????????????????????????????

  http://akizukidenshi.com/catalog/g/gM-06682/

  ?????????????????????????????????????????????????????

  ??????? ??? ???? ???

  http://i.stack.imgur.com/oOtkU.png

  PWM??????????????Pin

*/



#include <Servo.h>



Servo sv9;

Servo sv10;

Servo sv5;

Servo sv6;

int analog9 = 0;

int analog10 = 0;

int i = 7;

int inPin = 2;   // ??????2??????

int hallVal = 0;     // ?????????????

int lasthallVal = 0;     // ???????????????

int hallCount = 0; //?????????

unsigned long lastTime;

boolean servoAttached = false;



void moveShaft(Servo sv, int pulse, long int delay_ms)

{

  int pulse_now = sv.readMicroseconds();



  if ( pulse > pulse_now ) {

    for ( int i = pulse_now; i <= pulse; i++ ) {

      sv.writeMicroseconds(i);

      delay(delay_ms);

    }

  }

  else if ( pulse < pulse_now ) {

    for ( int i = pulse_now; i >= pulse; i-- ) {

      sv.writeMicroseconds(i);

      delay(delay_ms);

    }

  }

  else {

    // do nothing

  }

}



void setup()

{

  Serial.begin(9600);

  pinMode(13, OUTPUT); //LED??

  //???????????????? http://akizukidenshi.com/catalog/g/gI-05274/

  //??????????

  //???????????????????????? http://play-arduino.seesaa.net/article/427884258.html

  //Arduino ??? pinMode????2???INPUT_PULLUP http://mag.switch-science.com/2013/05/23/input_pullup/

  pinMode(inPin, INPUT_PULLUP);// ????????????

  lastTime = millis();

}



void loop()

{

  //TODO attachInterrupt(interrupt, function, mode) http://www.musashinodenpa.com/arduino/ref/index.php?f=0&pos=3045

  //Arduino Hall Effect Sensor Project http://diyhacking.com/projects/ArduinoHallEffect.ino

  hallVal = digitalRead(inPin);  // ???????

  if ( hallVal != lasthallVal) {

    lasthallVal = hallVal;

    if (hallVal == 1) {

      hallCount++;

    }

  }



  //Bt????

  if (servoAttached && lastTime > millis() + 1100) {

    sv9.writeMicroseconds(1500);

    sv10.writeMicroseconds(1500);

  }



  int ret;

  if ( Serial.available() > 0 ) {

    lastTime = millis();

    digitalWrite(13, HIGH); //LED??

    int d = Serial.read();



    if ( d == 'a' ) {

      sv9.attach(9, 800, 2200);

      sv10.attach(10, 800, 2200);

      sv5.attach(5, 800, 2200);

      sv6.attach(6, 800, 2200);

      servoAttached = true;

      Serial.println("Servo Attached");

      hallCount = 0;

    }

    else if ( d == 'd' ) {

      sv9.detach();

      sv10.detach();

      sv5.detach();

      sv6.detach();

      servoAttached = false;

      Serial.println("Servo Detached");

    }

    else if ( d == 'r' ) {

      if (hallCount != 0) {

        Serial.println("RPS:" + String(hallCount, DEC));

        //"Servo: " + String(sv9.read(), DEC) + " : " + String(sv10.read(), DEC));

        hallCount = 0;

      } else { //A0 Batt Volte

        int batValue = analogRead(A0);

        Serial.println("BAT:" + String(batValue, DEC));

      }

    }

    else if ( '0' <= d && d <= '9' ) {

      d -= '0';

      if (i == 7) {

        analog9 = d * 1000;

      }

      if (i == 6) {

        analog9 += d * 100;

      }

      if (i == 5) {

        analog9 += d * 10;

      }

      if (i == 4) {

        analog9 += d;

      }

      if (i == 3) {

        analog10 = d * 1000;

      }

      if (i == 2) {

        analog10 += d * 100;

      }

      if (i == 1) {

        analog10 += d * 10;

      }

      if (i == 0) {

        analog10 += d;

        //Serial.println("analog9  : " + String(analog9, DEC));

        //Serial.println("analog10 : " + String(analog10, DEC));

      }

      i--;

    }

    else if ( d == 'm' ) {

      sv9.writeMicroseconds(analog9);

      sv10.writeMicroseconds(analog10);

      //Serial.println("sv 9 Move to ms: " + String(analog9, DEC));

      //Serial.println("sv10 Move to ms: " + String(analog10, DEC));

      analog9 = 0;

      analog10 = 0;

      i = 7;

    } else if ( d == 'x' ) {

      //sv5.writeMicroseconds(analog9);

      moveShaft(sv5, analog9, 5);

      //Serial.println("camera x  : " + String(analog9, DEC));

      analog9 = 0;

      i = 7;

    } else if ( d == 'y' ) {

      //sv6.writeMicroseconds(analog9);

      moveShaft(sv6, analog9, 5);

      //Serial.println("camera y  : " + String(analog9, DEC));

      analog9 = 0;

      i = 7;

    }

    digitalWrite(13, LOW);   //LED??

  }

}
